# Fritzing sketch PC2 (saved by Fritzing 0.9.3b)
circuit board: 8.53488cm x 5.63626cm
breadboards: 1

parts:
  Componente2 = Adafruit FONA - Mini Cellular GSM Breakout
  Componente3 = Arduino Pro Mini v13

nets:
  N1: Componente2.VCCIO, Componente3.D3_PWM
  N2: Componente2.RXD_5V, Componente3.D4
  N3: Componente2.TXD_5V, Componente3.D5_PWM
  GND: Componente2.PWRKEY_5V, Componente2.GND, Componente3.GND
  N4: Componente2.RESET_5V, Componente3.D6_PWM

custom parts:
  Adafruit FONA - Mini Cellular GSM Breakout: An all-in-one cellular phone module that lets you add voice, text, SMS and GPRS data to your project. Quad-band 850/900/1800/1900MHz - connect onto any global GSM network with any 2G SIM. Includes an onboard LiPoly battery charging circuitry so you can take your project on the go. Also works as an FM radio receiver.
